// Digital circuit 2-bit-multiplier.dig as structural Verilog
module _2_bit_multiplier (
  input  A0,
  input  A1,
  input  B0,
  input  B1,
  output [3:0] out_5
);

  wire and_2_out, and_3_out, and_4_out, and_5_out;

  and and_1 (out_5[0], A0, B0);
  and and_2 (and_2_out, A0, B1);
  and and_3 (and_3_out, B0, A1);
  and and_4 (and_4_out, B1, A1);
  xor xor_1 (out_5[1], and_2_out, and_3_out);
  and and_5 (and_5_out, and_2_out, and_3_out);
  xor xor_2 (out_5[2], and_5_out, and_4_out);
  and and_6 (out_5[3], and_5_out, and_4_out);
endmodule
