// Digital circuit instruction-register.dig as structural Verilog
module instruction_register (
  input  [3:0] Input,
  input  Clock,
  input  [1:0] ctrl__LD_ST_CLR,
  input  crl__LD__ST,
  output [3:0] Output
);

  wire [3:0] multiplexer_1_out;

  Multiplexer #(.Bits(4)) multiplexer_1 (.sel(crl__LD__ST), .in_0(Output), .in_1(Input), .out(multiplexer_1_out));
  _4_bit_D_register _4_bit_d_register_1 (
    .Input(multiplexer_1_out), .ctrl__LD__ST__CLR(ctrl__LD_ST_CLR), .Clock(Clock), .Output(Output));
endmodule
