// Digital circuit 4-bit-D-register.dig as structural Verilog
module _4_bit_D_register (
  input  [3:0] Input,
  input  [1:0] ctrl__LD__ST__CLR,
  input  Clock,
  output [3:0] Output
);

  wire [3:0] multiplexer_1_out, not_1_out;

  assign not_1_out = ~4'b0000;  // Not not_1, 4 bits wide
  Multiplexer #(.Bits(4), .Selector_Bits(2)) multiplexer_1 (
    .sel(ctrl__LD__ST__CLR), .in_0(Output), .in_1(Input), .in_2(4'b0000), .in_3(not_1_out),
    .out(multiplexer_1_out));
  D_FF d_ff_1 (.D(multiplexer_1_out[3]), .C(Clock), .Q(Output[3]));  // open: nQ
  D_FF d_ff_2 (.D(multiplexer_1_out[2]), .C(Clock), .Q(Output[2]));  // open: nQ
  D_FF d_ff_3 (.D(multiplexer_1_out[1]), .C(Clock), .Q(Output[1]));  // open: nQ
  D_FF d_ff_4 (.D(multiplexer_1_out[0]), .C(Clock), .Q(Output[0]));  // open: nQ
endmodule
