// Digital circuit data-path-4-bit-processor.dig as structural Verilog
module data_path_4_bit_processor (
  input  clk,
  input  [1:0] pc_ctrl,
  input  [3:0] instr_mem_input,
  input  [1:0] intr_mem_ctrl,
  input  [1:0] IR_ctrl,
  output [1:0] pc_output,
  output [11:0] ir_output
);

  wire [3:0] _4_bit_memory_1_read, demultiplexer_1_out_0, demultiplexer_1_out_1, demultiplexer_1_out_2;
  wire [3:2] program_counter_1_output;

  program_counter program_counter_1 (
    .ctrl__LD__INC__RST(pc_ctrl), .Clock(clk), .Output({program_counter_1_output, pc_output}));
  _4_bit_memory _4_bit_memory_1 (
    .Address(pc_output), .Clock(clk), .Ctrl(intr_mem_ctrl), .Input(instr_mem_input),
    .Read(_4_bit_memory_1_read));
  Demultiplexer #(.Bits(4), .Selector_Bits(2)) demultiplexer_1 (
    .sel(pc_output), .in(_4_bit_memory_1_read), .out_0(demultiplexer_1_out_0), .out_1(demultiplexer_1_out_1),
    .out_2(demultiplexer_1_out_2));  // open: out_3
  instruction_register instruction_register_1 (
    .Input(demultiplexer_1_out_0), .Clock(clk), .ctrl__LD_ST_CLR(IR_ctrl), .Output(ir_output[3:0]));
  instruction_register instruction_register_2 (
    .Input(demultiplexer_1_out_1), .Clock(clk), .ctrl__LD_ST_CLR(IR_ctrl), .Output(ir_output[7:4]));
  instruction_register instruction_register_3 (
    .Input(demultiplexer_1_out_2), .Clock(clk), .ctrl__LD_ST_CLR(IR_ctrl), .Output(ir_output[11:8]));
endmodule
