// Digital circuit program-counter.dig as structural Verilog
module program_counter (
  input  [1:0] ctrl__LD__INC__RST,
  input  Clock,
  output [3:0] Output
);

  wire [3:0] _4_bit_adder_1_sum, multiplexer_1_out, not_1_out;

  _4_bit_adder _4_bit_adder_1 (.A(Output), .B(4'b0001), .Sum(_4_bit_adder_1_sum));  // open: Overflow_flag
  assign not_1_out = ~4'b0000;  // Not not_1, 4 bits wide
  Multiplexer #(.Selector_Bits(2), .Bits(4)) multiplexer_1 (
    .sel(ctrl__LD__INC__RST), .in_0(Output), .in_1(_4_bit_adder_1_sum), .in_2(4'b0000), .in_3(not_1_out),
    .out(multiplexer_1_out));
  D_FF d_ff_1 (.D(multiplexer_1_out[3]), .C(Clock), .Q(Output[3]));  // open: nQ
  D_FF d_ff_2 (.D(multiplexer_1_out[2]), .C(Clock), .Q(Output[2]));  // open: nQ
  D_FF d_ff_3 (.D(multiplexer_1_out[1]), .C(Clock), .Q(Output[1]));  // open: nQ
  D_FF d_ff_4 (.D(multiplexer_1_out[0]), .C(Clock), .Q(Output[0]));  // open: nQ
endmodule
