// Digital circuit register-file.dig as structural Verilog
module register_file (
  input  [1:0] Select_read1,
  input  [1:0] Select_read2,
  input  Clk,
  input  [3:0] Write_data,
  input  [1:0] Select_write,
  input  [7:0] Ctrl_registers,
  output [3:0] Read_data_1,
  output [3:0] Read_data_2
);

  wire [3:0] demultiplexer_1_out_0, demultiplexer_1_out_1, demultiplexer_1_out_2, demultiplexer_1_out_3,
       R_0_output, R_1_output, R_2_output, R_3_output;

  Demultiplexer #(.Bits(4), .Selector_Bits(2)) demultiplexer_1 (
    .sel(Select_write), .in(Write_data), .out_0(demultiplexer_1_out_0), .out_1(demultiplexer_1_out_1),
    .out_2(demultiplexer_1_out_2), .out_3(demultiplexer_1_out_3));
  _4_bit_D_register R_0 (
    .Input(demultiplexer_1_out_0), .ctrl__LD__ST__CLR(Ctrl_registers[1:0]), .Clock(Clk), .Output(R_0_output));
  _4_bit_D_register R_1 (
    .Input(demultiplexer_1_out_1), .ctrl__LD__ST__CLR(Ctrl_registers[3:2]), .Clock(Clk), .Output(R_1_output));
  _4_bit_D_register R_2 (
    .Input(demultiplexer_1_out_2), .ctrl__LD__ST__CLR(Ctrl_registers[5:4]), .Clock(Clk), .Output(R_2_output));
  _4_bit_D_register R_3 (
    .Input(demultiplexer_1_out_3), .ctrl__LD__ST__CLR(Ctrl_registers[7:6]), .Clock(Clk), .Output(R_3_output));
  Multiplexer #(.Bits(4), .Selector_Bits(2)) multiplexer_1 (
    .sel(Select_read1), .in_0(R_0_output), .in_1(R_1_output), .in_2(R_2_output), .in_3(R_3_output),
    .out(Read_data_1));
  Multiplexer #(.Selector_Bits(2), .Bits(4)) multiplexer_2 (
    .sel(Select_read2), .in_0(R_0_output), .in_1(R_1_output), .in_2(R_2_output), .in_3(R_3_output),
    .out(Read_data_2));
endmodule
