// Digital circuit 4-bit-adder-modified.dig as structural Verilog
module _4_bit_adder_modified (
  input  [3:0] A,
  input  [3:0] B,
  input  C_in,
  output [3:0] Sum,
  output Overflow_flag
);

  wire full_adder_curcuit_2_carry_out, full_adder_curcuit_3_carry_out, full_adder_curcuit_4_carry_out;

  Full_Adder_Curcuit full_adder_curcuit_1 (
    .A(A[3]), .B(B[3]), .Carry_in(full_adder_curcuit_2_carry_out), .Carry_out(Overflow_flag), .Sum(Sum[3]));
  Full_Adder_Curcuit full_adder_curcuit_2 (
    .A(A[2]), .B(B[2]), .Carry_in(full_adder_curcuit_3_carry_out),
    .Carry_out(full_adder_curcuit_2_carry_out), .Sum(Sum[2]));
  Full_Adder_Curcuit full_adder_curcuit_3 (
    .A(A[1]), .B(B[1]), .Carry_in(full_adder_curcuit_4_carry_out),
    .Carry_out(full_adder_curcuit_3_carry_out), .Sum(Sum[1]));
  Full_Adder_Curcuit full_adder_curcuit_4 (
    .A(A[0]), .B(B[0]), .Carry_in(C_in), .Carry_out(full_adder_curcuit_4_carry_out), .Sum(Sum[0]));
endmodule
