// Digital circuit 4-bit-memory.dig as structural Verilog
module _4_bit_memory (
  input  [1:0] Address,
  input  Clock,
  input  [1:0] Ctrl,
  input  [3:0] Input,
  output [3:0] Read
);

  wire and_1_out, and_2_out, and_3_out, and_4_out, decoder_1_out_0, decoder_1_out_1, decoder_1_out_2,
       decoder_1_out_3;
  wire [3:0] _4_bit_d_register_1_output, _4_bit_d_register_2_output, _4_bit_d_register_3_output,
       _4_bit_d_register_4_output;

  Decoder #(.Selector_Bits(2)) decoder_1 (
    .sel(Address), .out_0(decoder_1_out_0), .out_1(decoder_1_out_1), .out_2(decoder_1_out_2),
    .out_3(decoder_1_out_3));
  and and_1 (and_1_out, decoder_1_out_0, Clock);
  _4_bit_D_register _4_bit_d_register_1 (
    .Input(Input), .ctrl__LD__ST__CLR(Ctrl), .Clock(and_1_out), .Output(_4_bit_d_register_1_output));
  and and_2 (and_2_out, decoder_1_out_1, Clock);
  _4_bit_D_register _4_bit_d_register_2 (
    .Input(Input), .ctrl__LD__ST__CLR(Ctrl), .Clock(and_2_out), .Output(_4_bit_d_register_2_output));
  and and_3 (and_3_out, decoder_1_out_2, Clock);
  _4_bit_D_register _4_bit_d_register_3 (
    .Input(Input), .ctrl__LD__ST__CLR(Ctrl), .Clock(and_3_out), .Output(_4_bit_d_register_3_output));
  and and_4 (and_4_out, decoder_1_out_3, Clock);
  _4_bit_D_register _4_bit_d_register_4 (
    .Input(Input), .ctrl__LD__ST__CLR(Ctrl), .Clock(and_4_out), .Output(_4_bit_d_register_4_output));
  Multiplexer #(.Bits(4), .Selector_Bits(2)) multiplexer_1 (
    .sel(Address), .in_0(_4_bit_d_register_1_output), .in_1(_4_bit_d_register_2_output),
    .in_2(_4_bit_d_register_3_output), .in_3(_4_bit_d_register_4_output), .out(Read));
endmodule
