// Digital circuit data-path-4-bit-processor.dig as structural Verilog
module data_path_4_bit_processor (
  input  clk,
  input  [1:0] pc_ctrl,
  input  [3:0] instr_mem_input,
  input  [1:0] intr_mem_ctrl,
  input  [1:0] IR_ctrl,
  output [3:0] pc_output,
  output [15:0] ir_output,
  output alu_ctrl
);

  wire not_1_out, not_2_out;
  wire [1:0] demultiplexer_2_out_0, demultiplexer_2_out_1, demultiplexer_2_out_2, demultiplexer_2_out_3;
  wire [3:0] _16_bit_memory_1_p5, demultiplexer_1_out_0, demultiplexer_1_out_1, demultiplexer_1_out_2,
       demultiplexer_1_out_3, instruction_register_1_output, instruction_register_2_output,
       instruction_register_3_output, instruction_register_4_output;

  program_counter program_counter_1 (.ctrl__LD__INC__RST(pc_ctrl), .Clock(clk), .Output(pc_output));
  // _16_bit_memory _16_bit_memory_1: pin names not known; wires that end beside it: pc_output, instr_mem_input, intr_mem_ctrl, clk, _16_bit_memory_1_p5
  Demultiplexer #(.Selector_Bits(2), .Bits(4)) demultiplexer_1 (
    .sel(pc_output[1:0]), .in(_16_bit_memory_1_p5), .out_0(demultiplexer_1_out_0),
    .out_1(demultiplexer_1_out_1), .out_2(demultiplexer_1_out_2), .out_3(demultiplexer_1_out_3));
  Demultiplexer #(.Selector_Bits(2), .Bits(2)) demultiplexer_2 (
    .sel(pc_output[1:0]), .in(IR_ctrl), .out_0(demultiplexer_2_out_0), .out_1(demultiplexer_2_out_1),
    .out_2(demultiplexer_2_out_2), .out_3(demultiplexer_2_out_3));
  instruction_register instruction_register_1 (
    .Clock(clk), .ctrl__LD_ST_CLR(demultiplexer_2_out_0), .Load(demultiplexer_1_out_0),
    .Output(instruction_register_1_output));
  instruction_register instruction_register_2 (
    .Clock(clk), .ctrl__LD_ST_CLR(demultiplexer_2_out_1), .Load(demultiplexer_1_out_1),
    .Output(instruction_register_2_output));
  instruction_register instruction_register_3 (
    .Clock(clk), .ctrl__LD_ST_CLR(demultiplexer_2_out_2), .Load(demultiplexer_1_out_2),
    .Output(instruction_register_3_output));
  instruction_register instruction_register_4 (
    .Clock(clk), .ctrl__LD_ST_CLR(demultiplexer_2_out_3), .Load(demultiplexer_1_out_3),
    .Output(instruction_register_4_output));
  not not_1 (not_1_out, pc_output[0]);
  not not_2 (not_2_out, pc_output[1]);
  and and_1 (alu_ctrl, not_1_out, not_2_out);
  assign ir_output = alu_ctrl ? {instruction_register_4_output, instruction_register_3_output, instruction_register_2_output, instruction_register_1_output} : 16'bz;  // Driver driver_1
endmodule
