// Digital circuit instruction-register.dig as structural Verilog
module instruction_register (
  input  Clock,
  input  [1:0] ctrl__LD_ST_CLR,
  input  [3:0] Load,
  output [3:0] Output
);

  wire [3:0] multiplexer_1_out, not_1_out;

  assign not_1_out = ~4'b0000;  // Not not_1, 4 bits wide
  Multiplexer #(.Bits(4), .Selector_Bits(2)) multiplexer_1 (
    .sel(ctrl__LD_ST_CLR), .in_0(Output), .in_1(Load), .in_2(4'b0000), .in_3(not_1_out),
    .out(multiplexer_1_out));
  _4_bit_D_register _4_bit_d_register_1 (
    .Input(multiplexer_1_out), .ctrl__LD__ST__CLR(ctrl__LD_ST_CLR), .Clock(Clock), .Output(Output));
endmodule
