// Digital circuit register-file.dig as structural Verilog
module register_file (
  input  [1:0] Select_read1,
  input  [1:0] Select_read2,
  input  Clk,
  input  [3:0] Write_data,
  input  [1:0] Select_write,
  input  [7:0] Ctrl_registers,
  output [3:0] Read_data_1,
  output [3:0] Read_data_2
);

  wire [3:0] demultiplexer_1_out_0, demultiplexer_1_out_1, demultiplexer_1_out_2, demultiplexer_1_out_3,
       instruction_register_1_output, instruction_register_2_output, instruction_register_3_output,
       instruction_register_4_output;

  Demultiplexer #(.Selector_Bits(2), .Bits(4)) demultiplexer_1 (
    .sel(Select_write), .in(Write_data), .out_0(demultiplexer_1_out_0), .out_1(demultiplexer_1_out_1),
    .out_2(demultiplexer_1_out_2), .out_3(demultiplexer_1_out_3));
  instruction_register instruction_register_1 (
    .Clock(Clk), .ctrl__LD_ST_CLR(Ctrl_registers[1:0]), .Load(demultiplexer_1_out_0),
    .Output(instruction_register_1_output));
  instruction_register instruction_register_2 (
    .Clock(Clk), .ctrl__LD_ST_CLR(Ctrl_registers[3:2]), .Load(demultiplexer_1_out_1),
    .Output(instruction_register_2_output));
  instruction_register instruction_register_3 (
    .Clock(Clk), .ctrl__LD_ST_CLR(Ctrl_registers[5:4]), .Load(demultiplexer_1_out_2),
    .Output(instruction_register_3_output));
  instruction_register instruction_register_4 (
    .Clock(Clk), .ctrl__LD_ST_CLR(Ctrl_registers[7:6]), .Load(demultiplexer_1_out_3),
    .Output(instruction_register_4_output));
  Multiplexer #(.Selector_Bits(2), .Bits(4)) multiplexer_1 (
    .sel(Select_read1), .in_0(instruction_register_1_output), .in_1(instruction_register_2_output),
    .in_2(instruction_register_3_output), .in_3(instruction_register_4_output), .out(Read_data_1));
  Multiplexer #(.Selector_Bits(2), .Bits(4)) multiplexer_2 (
    .sel(Select_read2), .in_0(instruction_register_1_output), .in_1(instruction_register_2_output),
    .in_2(instruction_register_3_output), .in_3(instruction_register_4_output), .out(Read_data_2));
endmodule
