// Digital circuit assignment2-question7.dig as structural Verilog
module assignment2_question7 (
  input  I,
  input  Clk,
  output X
);

  wire and_1_out, and_2_out, FF1_nq, FF1_q, FF2_q;

  D_FF FF1 (.D(and_1_out), .C(Clk), .Q(FF1_q), .nQ(FF1_nq));
  and and_1 (and_1_out, FF1_nq, FF2_q);
  and and_2 (and_2_out, FF1_q, I, FF2_q);
  or or_1 (X, FF1_nq, FF2_q);
  D_FF FF2 (.D(and_2_out), .C(Clk), .Q(FF2_q));  // open: nQ
endmodule
